// Logisim project alu.circ as structural Verilog: 1 circuit, main circuit main
module main (
  input  Ctrl,
  input  Inc,
  input  A0,
  input  A1,
  input  B0,
  input  B1
);

  wire adder_1_cout, adder_1_out, adder_2_cout, adder_2_out, and_1_out, and_2_out, and_3_out, and_4_out,
       and_5_out, comparator_1_gt, comparator_2_eq, comparator_2_gt, nor_1_out, nor_2_out, nor_3_out,
       nor_4_out, not_1_out, not_2_out, or_1_out;

  nor nor_1 (nor_1_out, Ctrl, A0);
  nor nor_2 (nor_2_out, Ctrl, A1);
  nor nor_3 (nor_3_out, Ctrl, B0);
  nor nor_4 (nor_4_out, Ctrl, B1);
  and and_1 (and_1_out, Ctrl, A0);
  and and_2 (and_2_out, Ctrl, A1);
  and and_3 (and_3_out, Ctrl, B0);
  and and_4 (and_4_out, Ctrl, B1);
  not not_1 (not_1_out, nor_1_out);
  not not_2 (not_2_out, nor_2_out);
  Comparator #(.width(1)) comparator_1 (.a(and_1_out), .b(and_3_out), .gt(comparator_1_gt));  // open: eq, lt
  Comparator #(.width(1)) comparator_2 (
    .a(and_2_out), .b(and_4_out), .gt(comparator_2_gt), .eq(comparator_2_eq));  // open: lt
  Adder #(.width(1)) adder_1 (.a(not_1_out), .b(nor_3_out), .out(adder_1_out), .cin(Inc), .cout(adder_1_cout));
  Adder #(.width(1)) adder_2 (.a(not_2_out), .b(nor_4_out), .out(adder_2_out), .cin(adder_1_cout), .cout(adder_2_cout));
  and and_5 (and_5_out, comparator_1_gt, comparator_2_eq);
  LED led_1 (.in(adder_1_out));
  LED led_2 (.in(adder_2_out));
  LED led_3 (.in(adder_2_cout));
  or or_1 (or_1_out, and_5_out, comparator_2_gt);
  LED led_4 (.in(or_1_out));

  // Notes on the sheet:
  //   S0
  //   S1
  //   Cout
  //   Lt
endmodule
